# Fritzing sketch 2 (saved by Fritzing 0.9.4)
breadboards: 5

parts:
  IC1 = 74HC08 Logic AND Gate [part_number=74HC08 package="DIP (Dual Inline) [THT]"]  # not connected
  U1 = 74HC04_HEX_INVERTER [package=dil14]  # not connected
  S1 = SPST Switch [package=switch-spdt]
  S2 = SWITCH-MOMENTARY-2 [package=tactile-pth-12mm]  # not connected
  LED1 = smd LED [color="Red (633nm)" package="1206 [SMD]"]  # not connected
  S3 = SPST Switch [package=switch-spdt]
  S4 = SPST Switch [package=switch-spdt]
  S5 = SPST Switch [package=switch-spdt]
  S6 = SPST Switch [package=switch-spdt]
  S7 = SPST Switch [package=switch-spdt]
  S8 = SPST Switch [package=switch-spdt]
  S9 = SPST Switch [package=switch-spdt]
  S10 = SPST Switch [package=switch-spdt]
  VCC1 = Battery

nets:
  N1: S1.O, S3.O, S4.O, S5.O, S6.O, S7.O, S8.O, S9.O, S10.O, VCC1.+
  N2: S1.S, S3.S, S4.S, S5.S, S6.S, S7.S, S8.S, S9.S, S10.S, VCC1.-

notes:
  ]
  Cin
  B same as A
  A top to buttom S0 to S3
